# Fritzing sketch led_wave (saved by Fritzing 0.8.3b)
breadboards: 1

parts:
  R1 = Resistor [tolerance=±5% resistance=560 package=THT]
  R2 = Resistor [tolerance=±5% resistance=560 package=THT]
  R3 = Resistor [tolerance=±5% resistance=560 package=THT]
  R4 = Resistor [tolerance=±5% resistance=560 package=THT]
  R5 = Resistor [tolerance=±5% resistance=560 package=THT]
  LED3 = LED - 5mm [color="Red (633nm)" package="5 mm [THT]"]
  LED2 = LED - 5mm [color="Red (633nm)" package="5 mm [THT]"]
  LED1 = LED - 5mm [color="Red (633nm)" package="5 mm [THT]"]
  LED5 = LED - 5mm [color="Red (633nm)" package="5 mm [THT]"]
  LED4 = LED - 5mm [color="Red (633nm)" package="5 mm [THT]"]
  Part1 = Arduino Uno (Rev3)

nets:
  N1: R1.Pin_0, LED4.anode
  N2: R1.Pin_1, Part1.D2
  N3: R2.Pin_0, LED5.anode
  N4: R2.Pin_1, Part1.D6_PWM
  N5: R3.Pin_0, LED1.anode
  N6: R3.Pin_1, Part1.D5_PWM
  N7: R4.Pin_0, LED2.anode
  N8: R4.Pin_1, Part1.D4
  N9: R5.Pin_0, LED3.anode
  N10: R5.Pin_1, Part1.D3_PWM
  N11: LED3.cathode, LED2.cathode, LED1.cathode, LED5.cathode, LED4.cathode, Part1.GND
